# Fritzing sketch SchemaEmetteur (saved by Fritzing 0.9.3b)

parts:
  Composant1 = Arduino Pro Mini v13
  Composant2 = NRF24L01
  U1 = V_REG_LD1117VXX [package=78xxl]
  C1 = Electrolytic Capacitor [capacitance=47µF package="1010 [SMD, electrolytic]"]
  R1 = Rotary Potentiometer (Small) [maximum_resistance=100kΩ package=THT]
  R2 = Slide Potentiometer [maximum_resistance=100kΩ]
  R3 = Slide Potentiometer [maximum_resistance=100kΩ]
  R4 = Slide Potentiometer [maximum_resistance=100kΩ]
  R5 = Rotary Potentiometer (Small) [maximum_resistance=100kΩ package=THT]

nets:
  N1: Composant1.VCC, R1.leg2, R2.leg2, R3.leg2, R4.leg2, R5.leg2
  GND: Composant1.GND, Composant2.GND, U1.GND, C1.-, R1.leg1, R2.leg1, R3.leg1, R4.leg1, R5.leg1
  N2: Composant1.A4, R5.wiper
  5V: Composant1.RAW, U1.IN
  N3: Composant1.A3, R1.wiper
  N4: Composant1.A2, R2.wiper
  N5: Composant1.A1, R3.wiper
  N6: Composant1.A0, R4.wiper
  N7: Composant1.D13/SCK, Composant2.SCK
  N8: Composant1.D12/MISO, Composant2.MISO
  N9: Composant1.D11_PWM/MOSI, Composant2.MOSI
  N10: Composant1.D10_PWM/SS, Composant2.CSN
  N11: Composant1.D9_PWM, Composant2.CE
  N12: Composant2.VCC, U1.OUT, C1.+
