# Fritzing sketch SchemaRecepteur (saved by Fritzing 0.9.3b)

parts:
  Composant1 = Adafruit PCA9685 PWM/Servo Breakout [part_number=815]
  Composant3 = NRF24L01
  J1 = Basic Servo
  J2 = Basic Servo
  J3 = Basic Servo
  J4 = Basic Servo
  M1 = DC Motor
  Q1 = TRANSISTOR_NPN [package=to-92-ammo]
  Composant4 = Arduino Pro Mini v13
  C1 = Electrolytic Capacitor [capacitance=47µF package="1010 [SMD, electrolytic]"]
  U1 = V_REG_LD1117VXX [package=78xxl]
  VCC1 = Battery block 9V
  D1 = Diode [package=sma-diode_alt]

nets:
  5V: Composant1.5.0V, J1.vcc, J2.vcc, J3.vcc, J4.vcc, Composant4.RAW, U1.IN
  GND: Composant1.GND, Composant3.GND, J1.gnd, J2.gnd, J3.gnd, J4.gnd, Composant4.GND, C1.-, U1.GND
  N1: Composant1.PWM4, Q1.B
  N2: Composant1.PWM3, J4.pulse
  N3: Composant1.PWM2, J3.pulse
  N4: Composant1.PWM1, J2.pulse
  N5: Composant1.PWM0, J1.pulse
  VCC: Composant1.VCC, Composant4.VCC
  N6: Composant1.SDA, Composant4.A4
  N7: Composant1.SCL, Composant4.A5
  N8: Composant3.MOSI, Composant4.D11_PWM/MOSI
  N9: Composant3.CSN, Composant4.D10_PWM/SS
  N10: Composant3.VCC, C1.+, U1.OUT
  N11: Composant3.MISO, Composant4.D12/MISO
  N12: Composant3.SCK, Composant4.D13/SCK
  N13: Composant3.CE, Composant4.D9_PWM
  N14: M1.pin_1, Q1.E, D1.C
  N15: M1.pin_2, VCC1.-, D1.A
  N16: Q1.C, VCC1.+

custom parts:
  Adafruit PCA9685 PWM/Servo Breakout: Using only two pins, control 16 free-running PWM outputs! I2C-controlled PWM driver with a built in clock. Unlike the TLC5940 family, you do not need to continuously send it signal tying up your microcontroller, its completely free running! 5V compliant, which means you can control it from a 3.3V microcontroller and still safely drive up to 6V outputs (this is good for when you want to control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
